# Fritzing sketch BedLed (saved by Fritzing 0.9.3b)
circuit board: 2.37752cm x 2.18248cm
breadboards: 1

parts:
  Q1 = MOSFET-NCHANNEL [part_number=IRFZ44N package=to220v]
  IC2 = Voltage Regulator [part_number=LM7805 package=to220-igo]
  U1 = attiny85 [package=dip]
  R1 = Resistor [tolerance=±5% resistance=10M package=THT]
  C1 = Ceramic Capacitor [capacitance=0.33µF voltage=16V package="100 mil [THT, multilayer]"]
  C2 = Ceramic Capacitor [capacitance=0.1µF package="100 mil [THT, multilayer]"]
  Sense = Screw terminal - 2 pins [package=THT]
  C3 = Ceramic Capacitor [capacitance=10pF package="100 mil [THT, multilayer]"]
  IN = Screw terminal - 2 pins [package=THT]
  D1 = Schottky Diode [part_number=SB5100 package="300 mil [THT]"]
  LED = Screw terminal - 2 pins [package=THT]

nets:
  N1: Q1.G, U1.Pin_5
  N2: Q1.D, LED.pin2
  GND: Q1.S, IC2.GND, U1.Pin_4, C1.0, C2.1, Sense.pin1, C3.1, IN.pin2
  12V: IC2.IN, C1.1, D1.cathode, LED.pin1
  5V: IC2.OUT, U1.Pin_8, C2.0
  N3: U1.Pin_2, R1.Pin_1
  N4: U1.Pin_3, R1.Pin_0, Sense.pin2, C3.0
  N5: IN.pin1, D1.anode

notes:
  Power Management
  LED Control
  Cap. Sensing
  9-20V ≤3A
  PWR
  LED
  SENS
  Chris van Marle
  +
  -
  IN
  Sense
  BedLed 2016
  ⏚
  ⍑
  12V+
